# Fritzing sketch schematic (saved by Fritzing 0.9.3b)
breadboards: 1

parts:
  GYRO = Triple Axis Magnetometer - HMC5883 Breakout
  RB = TQFP32-5MM [chip_label=RedBoard package=TQFP]
  RECEIVER_OUTPUT = optical jack orj-8 [package=tht]
  ESC = SO18W [chip_label=ESC package=SO(w)]
  Vbat = Battery Holders [package=battery-aa]

nets:
  GND: GYRO.GND, RB.GND
  VCC: GYRO.VCC, RB.5V
  N1: GYRO.SDA, RB.SDA
  N2: GYRO.SCL, RB.SCL
  N3: RB.4, ESC.1
  N4: RB.~5, ESC.2
  N5: RB.~6, ESC.3
  N6: RB.7, ESC.4
  N7: RB.8, RECEIVER_OUTPUT.pin5
  N8: RB.~9, RECEIVER_OUTPUT.pin4
  N9: RB.~10, RECEIVER_OUTPUT.pin3
  N10: RB.~11, RECEIVER_OUTPUT.pin2
  N11: RB.12, RECEIVER_OUTPUT.pin1
  N12: ESC.5, Vbat.-
  N13: ESC.6, Vbat.+
